// Logisim project Jean-Implementations.circ as structural Verilog: 1 circuit, main circuit main
module main (
  input  in_1,
  input  Jump_Enable,
  input  [31:0] in_3,
  output [31:0] PC_Content
);

  wire Reset;
  wire [31:0] adder_1_out, and_1_out, multiplexer_1_out;

  assign and_1_out = in_3 & 32'hfffffffc;  // AND_Gate and_1, 32 bits wide
  Multiplexer #(.width(32)) multiplexer_1 (
    .in0(adder_1_out), .in1(and_1_out), .out(multiplexer_1_out), .sel(Jump_Enable));  // open: en
  Button button_1 (.out(Reset));
  Register #(.width(32)) Registro (.D(multiplexer_1_out), .Q(PC_Content), .clk(in_1), .clr(Reset));  // open: en
  Adder #(.width(32)) adder_1 (.a(PC_Content), .b(32'h4), .out(adder_1_out));  // open: cin, cout
  // Probe on PC_Content

  // Other names for the same wires on the sheet: CLK = in_1
endmodule
